// Digital circuit alu_test.dig as structural Verilog
module alu_test (
  input  [3:0] alu_operator,
  input  [31:0] alu_b,
  input  [31:0] alu_a,
  output [31:0] alu_result,
  output alu_zero,
  output alu_overflow,
  output alu_carry,
  output alu_negative,
  output alu_parity
);

  hyaena_alu #(.applicationType("IVERILOG"), .CodeFile("/home/erdem/hyaena/rtl/hyaena_alu.v")) u_hyaena_alu (
    .operator(alu_operator), .a(alu_a), .b(alu_b), .result(alu_result), .zero(alu_zero),
    .overflow(alu_overflow), .carry(alu_carry), .negative(alu_negative), .parity(alu_parity));

  // Notes on the sheet:
  //   alu_result: ALU
  //   alu_zero: ALU
  //   alu_overflow: ALU
  //   alu_carry: ALU
  //   alu_negative: ALU
  //   alu_parity: ALU
  //   alu_operator: ALU
  //   alu_b: ALU
  //   alu_a: ALU
endmodule
